# Fritzing sketch Circuit_MPU6050_MicroPro (saved by Fritzing 1.0.1rc)
breadboards: 1

parts:
  Part1 = Arduino Pro Micro (Clone)
  Part2 = InvenSense MPU6050

nets:
  N1: Part1.D2, Part2.SDA
  N2: Part1.D3, Part2.SCL
